// Logisim project feataku.circ as structural Verilog
// SC
module SemiSumador (
  input  X,
  input  Y,
  input  CIn,
  output S,
  output COut
);

  wire and_1_out, and_2_out, xor_1_out;

  xor xor_1 (xor_1_out, X, Y);
  and and_1 (and_1_out, X, Y);
  xor xor_2 (S, xor_1_out, CIn);
  and and_2 (and_2_out, xor_1_out, CIn);
  xor xor_3 (COut, and_2_out, and_1_out);
endmodule

module Sumador4Bits (
  input  in_1,
  input  in_2,
  input  in_3,
  input  in_4,
  input  in_5,
  input  in_6,
  input  in_7,
  input  in_8,
  input  in_9,
  output out_10,
  output out_11,
  output out_12,
  output out_13,
  output out_14
);

  wire semisumador_1_cout, semisumador_2_cout, semisumador_3_cout;

  SemiSumador semisumador_1 (.X(in_1), .Y(in_2), .CIn(in_3), .S(out_10), .COut(semisumador_1_cout));
  SemiSumador semisumador_2 (.X(in_4), .Y(in_5), .CIn(semisumador_1_cout), .S(out_11), .COut(semisumador_2_cout));
  SemiSumador semisumador_3 (.X(in_6), .Y(in_7), .CIn(semisumador_2_cout), .S(out_12), .COut(semisumador_3_cout));
  SemiSumador semisumador_4 (.X(in_8), .Y(in_9), .CIn(semisumador_3_cout), .S(out_13), .COut(out_14));
endmodule
